// Logisim project full_adder.circ as structural Verilog: 1 circuit, main circuit main
module main (
  input  B,
  input  A,
  input  Cin,
  output Cout,
  output S
);

  wire and_1_out, and_2_out, and_3_out;

  and and_1 (and_1_out, A, B);
  and and_2 (and_2_out, B, Cin);
  and and_3 (and_3_out, Cin, A);
  or or_1 (Cout, and_1_out, and_2_out, and_3_out);
  ExactlyOne xor_1 (.out(S), .in0(B), .in2(Cin), .in4(A));
endmodule
